# Fritzing sketch final 회로도 (saved by Fritzing 0.9.3b)
breadboards: 1

parts:
  부품1 = Arduino Uno (Rev3)
  부품2 = 9 Degrees of Freedom - Sensor Stick

nets:
  N1: 부품1.A4/SDA, 부품2.SDA
  N2: 부품1.A5/SCL, 부품2.SCL
  5V: 부품1.5V, 부품2.VCC
  GND: 부품1.GND, 부품2.GND

notes:
  Gyrosensor IMU 9DOF
